# Fritzing sketch patient monitoring (saved by Fritzing 0.9.5d)
breadboards: 2

parts:
  Grove1 = Grove OLED 128x96
  S1 = Round Pushbutton
  S2 = Round Pushbutton
  R1 = Resistor [tolerance=±5% resistance=220 package="1206 [SMD]"]
  R2 = Resistor [tolerance=±5% resistance=220 package="0402 [SMD]"]
  LED1 = smd LED [color="Red (633nm)" package="1206 [SMD]"]
  R3 = Resistor [tolerance=±5% resistance=220 package="1206 [SMD]"]
  LED2 = smd LED [color="Red (633nm)" package="1206 [SMD]"]
  R4 = Resistor [tolerance=±5% resistance=220 package="1206 [SMD]"]
  LED3 = smd LED [color="Red (633nm)" package="1206 [SMD]"]
  R5 = Resistor [tolerance=±5% resistance=220 package="1206 [SMD]"]
  DS1 = DS18B20 1-Wire Temperature Sensor Probe
  A1 = u-blox NEO-6M GPS Breakout
  U3 = ESP8266 NodeMCU LoLin module
  M1 = MAX30102
  J1 = Piezo Speaker
  R8 = Resistor [tolerance=±5% resistance=220 package="1206 [SMD]"]
  F1 = Fan - Ventilador [package=THT]
  VCC1 = Battery
  R9 = Resistor [tolerance=±5% resistance=220 package="1206 [SMD]"]
  R10 = Resistor [tolerance=±5% resistance=220 package="1206 [SMD]"]
  U4 = SWITCH_SPDT [package=kps-1290]

nets:
  GND: Grove1.GND, R1.Pin_1, R2.Pin_0, DS1.GND, A1.Pin_2, U3.GND, M1.GND, J1.pin1, F1.GND, VCC1.-
  VCC: Grove1.VCC, DS1.VDD, A1.Pin_1, U3.3V3, M1.VIN, R8.Pin_1, F1.5V
  N1: Grove1.SDA, M1.SDA
  N2: Grove1.SCL, M1.SCL
  N3: S1.leg0, S2.leg1, LED1.cathode, VCC1.+, R9.Pin_0, R10.Pin_1, U4.S
  N4: S1.leg1, R2.Pin_1, U3.D5
  N5: S2.leg0, R1.Pin_0, U3.D6
  N6: LED1.anode, R3.Pin_0
  N7: R3.Pin_1, R4.Pin_1, R5.Pin_1
  N8: LED2.anode, R4.Pin_0
  N9: LED3.anode, R5.Pin_0
  N10: DS1.DQ, U3.D4, R8.Pin_0
  N11: A1.Pin_3, U3.D7
  N12: A1.Pin_4, U3.D8
  N13: U3.D0, M1.INT
  N14: U3.D3, J1.pin2
  N15: U3.A0, U4.P
  N16: R9.Pin_1, U4.O

custom parts:
  ESP8266 NodeMCU LoLin module: ESP8266 based NodeMCU
  MAX30102: Oximeter module using the MAX30102 chip. You may wish to read (and check your module) this post on power problems with these modules: https://reedpaper.wordpress.com/2018/08/22/pulse-oximeter-max30100-max30102-how-to-fix-wrong-board/ . As usual, if you want the mounting holes in pcb, you need to drag a hole over the pad in silkscreen to actually drill the hole (by default they are not drilled)
  Fan - Ventilador: Ventilador de 2 pines, se encuentra comunmente en computadoras de escritorio
